# Fritzing sketch circuit (saved by Fritzing 0.9.3b)

parts:
  Part1 = Arduino Nano (Rev3.0) (ICSP)
  HC-SR04_Sensor_1 = HC-SR04 Ultrasonic Distance Sensor
  Part2 = Bluetooth HC-05 Macho
  U2 = LIPO-2000mAh [package=lipo-2000]
  U3 = Vibration Motor- ROB-08449 [package=vibe-motor-10mm]
  IC1 = L293D [package=THT]
  Part3 = Power Cell LiPo Charger/Booster
  USB_A = USB Connectors [package=usb-minib]
  USB_MINI-B = USB Connectors [package=usb-a-h]
  S1 = SWITCH-MOMENTARY-2 [package=tactile-switch-1101ne]
  S2 = SWITCH-MOMENTARY-2 [package=tactile_switch_smd-2]
  S3 = SWITCH-MOMENTARY-2 [package=tactile_switch_smd-2]
  S4 = SWITCH-MOMENTARY-2 [package=tactile_switch_smd-2]
  S5 = SWITCH-MOMENTARY-2 [package=tactile_switch_smd-2]
  R1 = Resistor [tolerance=±5% resistance=220 package="0402 [SMD]"]
  R2 = Resistor [tolerance=±5% resistance=220 package="0402 [SMD]"]
  R3 = Resistor [tolerance=±5% resistance=220 package="0402 [SMD]"]
  R4 = Resistor [tolerance=±5% resistance=220 package="0402 [SMD]"]
  U1 = Vibration Motor- ROB-08449 [package=vibe-motor-10mm]
  LED1 = smd LED [color="Red (633nm)" package="0603 [SMD]"]
  S6 = SWITCH-MOMENTARY-2 [package=tactile_switch_smd-2]
  R5 = Resistor [tolerance=±5% resistance=220 package="0402 [SMD]"]
  J1 = Piezo Speaker

nets:
  N1: Part1.D1/TX, LED1.anode
  N2: Part1.D2, Part2.State
  N3: Part1.D3, Part2.TXD
  N4: Part1.D4, Part2.RXD
  N5: Part1.D5, IC1.In_1, IC1.In_2
  N6: Part1.D6, J1.pin2
  N7: Part1.D7, HC-SR04_Sensor_1.TRIG
  N8: Part1.D8, HC-SR04_Sensor_1.GND
  N9: Part1.D9, S4.2, R1.Pin_0
  N10: Part1.D10, S2.2, R3.Pin_0
  N11: Part1.D11/MOSI, S3.2, R2.Pin_0
  N12: Part1.D12/MISO, S5.2, R4.Pin_0
  N13: Part1.VIN, S1.2
  GND: Part1.GND, HC-SR04_Sensor_1.ECHO, Part2.GND, U2.-, U3.-, IC1.0V, Part3.GND, USB_A.GND, USB_MINI-B.GND, R1.Pin_1, R2.Pin_1, R3.Pin_1, R4.Pin_1, U1.-, LED1.cathode, R5.Pin_1, J1.pin1
  VCC: Part1.5V, HC-SR04_Sensor_1.VCC, Part2.VCC, IC1.Enable_1, IC1.+V, S4.1
  N14: Part1.A0, U2.+, Part3.VBATT
  N15: Part1.D13/SCK, S6.2, R5.Pin_0
  N16: U3.+, IC1.Out_2_(_Controlled_by_Enable_1_)
  N17: IC1.Out_1_(_Controlled_by_Enable_1_), U1.+
  N18: Part3.VCC, USB_A.D+
  N19: Part3.5VIN, USB_MINI-B.D+
  N20: S2.1, S3.1, S5.1, S6.1
